# Fritzing sketch wireless-programable-motor (saved by Fritzing 0.9.1b)

parts:
  Part1 = Arduino Uno (Rev3) - ICSP
  Part2 = EasyDriver_v44
  Part3 = Bluetooth Mate Silver
  M1 = Stepper Motor - Bipolar

nets:
  5V: Part1.5V, Part3.VCC
  GND: Part1.GND, Part2.GND, Part3.GND
  N1: Part1.D2, Part2.DIR
  N2: Part1.D3_PWM, Part2.STEP
  N3: Part1.D4, Part3.TX_5V
  N4: Part1.D5_PWM, Part3.RX_5V
  N5: Part1.VIN, Part2.V+
  N6: Part2.OUT2A, M1.A
  N7: Part2.OUT2B, M1.C
  N8: Part2.OUT1A, M1.B
  N9: Part2.OUT1B, M1.D

notes:
  12 VDC Power Supply
  Stepper Motor
  Bluetooth Mate Silver
  Easy Driver
